# Fritzing sketch Auto_wiper (saved by Fritzing 0.9.2b)
breadboards: 1

parts:
  C1 = Electrolytic Capacitor [capacitance=1µF package="100 mil [THT, electrolytic]"]
  C2 = Electrolytic Capacitor [capacitance=1µF package="100 mil [THT, electrolytic]"]
  C3 = Ceramic Capacitor [capacitance=10pF package="100 mil [THT, multilayer]"]
  IC1 = IC, DIP package, 16 pins [chip_label=L293D spacing=300mil]
  M1 = DC Motor
  VCC1 = Battery block 9V
  Arduino1 = Arduino Uno (Rev3)
  LCD1 = LCD screen
  U1 = Voltage Regulator - 5V [package="TO220 [THT]"]
  R1 = Trimmer Potentiometer [maximum_resistance=10kΩ package=THT]
  J1 = screw terminal, 3 pins

nets:
  VSS: C1.-, C2.-, C3.0, IC1.pin4, IC1.pin5, IC1.pin12, IC1.pin13, VCC1.-, LCD1.VSS, LCD1.R/W, U1.GND, R1.leg2, J1.pin3
  N1: C1.+, VCC1.+, U1.input_voltage
  N2: C2.+, C3.1, IC1.pin1, IC1.pin8, IC1.pin16, LCD1.VDD, U1.output_voltage, R1.leg1, J1.pin1
  N3: IC1.pin2, Arduino1.D7
  N4: IC1.pin3, M1.pin_1
  N5: IC1.pin6, M1.pin_2
  N6: IC1.pin7, Arduino1.D6_PWM
  N7: Arduino1.A0, J1.pin2
  N8: Arduino1.D8, LCD1.DB7
  N9: Arduino1.D9_PWM, LCD1.DB6
  N10: Arduino1.D10_PWM/SS, LCD1.DB5
  N11: Arduino1.D11_PWM/MOSI, LCD1.DB4
  N12: Arduino1.D12/MISO, LCD1.E
  N13: Arduino1.D13/SCK, LCD1.RS
  N14: LCD1.V0, R1.wiper
